# Fritzing sketch AIT Final Diagram (saved by Fritzing 0.9.3b)
breadboards: 1

parts:
  VM+ = Header 1 [package=luxeon-pad]
  Vcc = Header 1 [package=luxeon-pad]
  Gnd = Header 1 [package=luxeon-pad]
  PWMB = Header 1 [package=luxeon-pad]
  BIN2 = Header 1 [package=luxeon-pad]
  BIN1 = Header 1 [package=luxeon-pad]
  STBY = Header 1 [package=luxeon-pad]  # not connected
  AIN1 = Header 1 [package=luxeon-pad]
  AIN2 = Header 1 [package=luxeon-pad]
  PWMA = Header 1 [package=luxeon-pad]
  MOTORB = Header 1 [package=luxeon-pad]
  MOTORB_2 = Header 1 [package=luxeon-pad]
  GND = Header 1 [package=luxeon-pad]  # not connected
  GND_2 = Header 1 [package=luxeon-pad]  # not connected
  MOTORA = Header 1 [package=luxeon-pad]
  MOTORA_2 = Header 1 [package=luxeon-pad]
  VM+_2 = Header 1 [package=luxeon-pad]
  Vcc_2 = Header 1 [package=luxeon-pad]
  Gnd_2 = Header 1 [package=luxeon-pad]
  PWMB_2 = Header 1 [package=luxeon-pad]
  BIN2_2 = Header 1 [package=luxeon-pad]
  BIN1_2 = Header 1 [package=luxeon-pad]
  AIN2_2 = Header 1 [package=luxeon-pad]
  STBY_2 = Header 1 [package=luxeon-pad]  # not connected
  PWMA_2 = Header 1 [package=luxeon-pad]
  AIN1_2 = Header 1 [package=luxeon-pad]
  MOTORA_3 = Header 1 [package=luxeon-pad]
  GND_3 = Header 1 [package=luxeon-pad]  # not connected
  MOTORB_3 = Header 1 [package=luxeon-pad]
  GND_4 = Header 1 [package=luxeon-pad]  # not connected
  MOTORA_4 = Header 1 [package=luxeon-pad]
  MOTORB_4 = Header 1 [package=luxeon-pad]
  Part1 = Arduino Uno (Rev3)
  JP2 = Header 1 [package=luxeon-pad]
  part = Header 1 [package=luxeon-pad]
  PWR = Header 1 [package=luxeon-pad]
  GND_5 = Header 1 [package=luxeon-pad]
  Button_1_In = Header 1 [package=luxeon-pad]
  Button_1_Out = Header 1 [package=luxeon-pad]
  Button_2_In = Header 1 [package=luxeon-pad]
  Button_2_Out = Header 1 [package=luxeon-pad]
  GND_6 = Header 1 [package=luxeon-pad]
  VCC = Header 1 [package=luxeon-pad]
  PWM = Header 1 [package=luxeon-pad]
  Blue_Button-_liquid = Pushbutton [package="[THT]"]
  Green_Button-_solid = Pushbutton [package="[THT]"]
  Servo = Basic Servo
  PUSH_motor = Stepper Motor - Bipolar
  LIFT_motor = Stepper Motor - Bipolar

nets:
  VIN: VM+.1, Vcc.1, PWMB.1, PWMA.1, VM+_2.1, Vcc_2.1, PWMB_2.1, PWMA_2.1, Part1.D2, Part1.D3_PWM, Part1.VIN, JP2.1, part.1, PWR.1, Button_1_In.1, Button_1_Out.1, Button_2_In.1, Button_2_Out.1, VCC.1, Blue_Button-_liquid.Pin_1, Blue_Button-_liquid.Pin_2, Green_Button-_solid.Pin_1, Green_Button-_solid.Pin_2, Servo.vcc
  N1: Gnd.1, Gnd_2.1, Part1.GND, Part1.D0/RX, Part1.D1/TX, GND_5.1, Blue_Button-_liquid.Pin_3, Blue_Button-_liquid.Pin_4, Green_Button-_solid.Pin_3, Green_Button-_solid.Pin_4
  N2: BIN2.1, Part1.D11_PWM/MOSI
  N3: BIN1.1, Part1.D10_PWM/SS
  N4: AIN1.1, Part1.D9_PWM
  N5: AIN2.1, Part1.D8
  N6: MOTORB.1, PUSH_motor.A
  N7: MOTORB_2.1, PUSH_motor.C
  N8: MOTORA.1, PUSH_motor.B
  N9: MOTORA_2.1, PUSH_motor.D
  N10: BIN2_2.1, Part1.D7
  N11: BIN1_2.1, Part1.D6_PWM
  N12: AIN2_2.1, Part1.D4
  N13: AIN1_2.1, Part1.D5_PWM
  N14: MOTORA_3.1, LIFT_motor.B
  N15: MOTORB_3.1, LIFT_motor.C
  N16: MOTORA_4.1, LIFT_motor.D
  N17: MOTORB_4.1, LIFT_motor.A
  N18: Part1.D12/MISO, PWM.1, Servo.pulse
  N19: GND_6.1, Servo.gnd

notes:
  TB6612
  Stepper Motor Wiring in order from PUSH Motor MOTORB --> LIFT motor MOTORA
  Black/Red/White
  Grey
  Brown/Purple/White
  Orange/White
  Blue/Black
  Purple
  Green/Black
  Blue
  Although the wire color is accurate, the connection to servo is not accurate.
