# Fritzing sketch ARIA_final_diagram (saved by Fritzing 0.9.3b)
breadboards: 1

parts:
  VM+ = Header 1 [package=luxeon-pad]
  Vcc = Header 1 [package=luxeon-pad]
  Gnd = Header 1 [package=luxeon-pad]
  PWMB = Header 1 [package=luxeon-pad]
  BIN2 = Header 1 [package=luxeon-pad]
  BIN1 = Header 1 [package=luxeon-pad]
  STBY = Header 1 [package=luxeon-pad]  # not connected
  AIN1 = Header 1 [package=luxeon-pad]
  AIN2 = Header 1 [package=luxeon-pad]
  PWMA = Header 1 [package=luxeon-pad]
  MOTORB_(Red/Black/White) = Header 1 [package=luxeon-pad]
  MOTORB_(Grey) = Header 1 [package=luxeon-pad]
  GND = Header 1 [package=luxeon-pad]  # not connected
  GND_2 = Header 1 [package=luxeon-pad]  # not connected
  MOTORA_(Brown/Purple/White) = Header 1 [package=luxeon-pad]
  MOTORA_(Orange/White) = Header 1 [package=luxeon-pad]
  VM+_2 = Header 1 [package=luxeon-pad]
  Vcc_2 = Header 1 [package=luxeon-pad]
  Gnd_2 = Header 1 [package=luxeon-pad]
  PWMB_2 = Header 1 [package=luxeon-pad]
  BIN2_2 = Header 1 [package=luxeon-pad]
  BIN1_2 = Header 1 [package=luxeon-pad]
  AIN2_2 = Header 1 [package=luxeon-pad]
  STBY_2 = Header 1 [package=luxeon-pad]  # not connected
  PWMA_2 = Header 1 [package=luxeon-pad]
  AIN1_2 = Header 1 [package=luxeon-pad]
  MOTORA_(Green/Black) = Header 1 [package=luxeon-pad]
  GND_3 = Header 1 [package=luxeon-pad]  # not connected
  MOTORB_(Purple) = Header 1 [package=luxeon-pad]
  GND_4 = Header 1 [package=luxeon-pad]  # not connected
  MOTORA_(Blue) = Header 1 [package=luxeon-pad]
  MOTORB_(Blue/Black) = Header 1 [package=luxeon-pad]
  Part1 = Arduino Uno (Rev3)
  JP2 = Header 1 [package=luxeon-pad]
  JP3 = Header 1 [package=luxeon-pad]
  PWR = Header 1 [package=luxeon-pad]
  GND_5 = Header 1 [package=luxeon-pad]
  Button_1_In_(Orange) = Header 1 [package=luxeon-pad]
  Button_1_Out_(Red) = Header 1 [package=luxeon-pad]
  Button_2_In_(Brown) = Header 1 [package=luxeon-pad]
  Button_2_Out_(Black) = Header 1 [package=luxeon-pad]
  GND_(Orange) = Header 1 [package=luxeon-pad]
  VCC_(Green) = Header 1 [package=luxeon-pad]
  PWM_(yellow) = Header 1 [package=luxeon-pad]
  Blue_Button-_liquid = Pushbutton [package="[THT]"]
  Green_Button-_solid = Pushbutton [package="[THT]"]
  Servo = Basic Servo
  PUSH_motor = Stepper Motor - Bipolar
  LIFT_motor = Stepper Motor - Bipolar
  part = Resistor [tolerance=±5% resistance=10k package="0603 [SMD]"]
  part_2 = Resistor [tolerance=±5% resistance=10k package="0603 [SMD]"]

nets:
  VIN: VM+.1, Vcc.1, PWMB.1, PWMA.1, VM+_2.1, Vcc_2.1, PWMB_2.1, PWMA_2.1, Part1.D2, Part1.D3_PWM, Part1.VIN, JP2.1, JP3.1, PWR.1, Button_1_In_(Orange).1, Button_1_Out_(Red).1, Button_2_In_(Brown).1, Button_2_Out_(Black).1, VCC_(Green).1, Blue_Button-_liquid.Pin_1, Blue_Button-_liquid.Pin_2, Green_Button-_solid.Pin_1, Green_Button-_solid.Pin_2, Servo.vcc, part.Pin_0, part_2.Pin_0
  GND: Gnd.1, Gnd_2.1, Part1.GND, Part1.D0/RX, Part1.D1/TX, GND_5.1, GND_(Orange).1, Blue_Button-_liquid.Pin_3, Blue_Button-_liquid.Pin_4, Green_Button-_solid.Pin_3, Green_Button-_solid.Pin_4, Servo.gnd, part.Pin_1
  N1: BIN2.1, Part1.D11_PWM/MOSI
  N2: BIN1.1, Part1.D10_PWM/SS
  N3: AIN1.1, Part1.D9_PWM
  N4: AIN2.1, Part1.D8
  N5: MOTORB_(Red/Black/White).1, PUSH_motor.A
  N6: MOTORB_(Grey).1, PUSH_motor.C
  N7: MOTORA_(Brown/Purple/White).1, PUSH_motor.B
  N8: MOTORA_(Orange/White).1, PUSH_motor.D
  N9: BIN2_2.1, Part1.D7
  N10: BIN1_2.1, Part1.D6_PWM
  N11: AIN2_2.1, Part1.D4
  N12: AIN1_2.1, Part1.D5_PWM
  N13: MOTORA_(Green/Black).1, LIFT_motor.B
  N14: MOTORB_(Purple).1, LIFT_motor.C
  N15: MOTORA_(Blue).1, LIFT_motor.D
  N16: MOTORB_(Blue/Black).1, LIFT_motor.A
  N17: Part1.D12/MISO, PWM_(yellow).1, Servo.pulse

notes:
  TB6612
  Although the wire color is accurate, the connection to servo is not accurate.
