# Fritzing sketch ARIA Final Wiring (saved by Fritzing 0.9.3b)
breadboards: 1

parts:
  Part1 = Arduino Uno (Rev3)
  Push = Motor Driver 1A Dual TB6612FNG
  Lift = Motor Driver 1A Dual TB6612FNG
  Lift_2 = Stepper Motor - Unipolar
  Push_2 = Stepper Motor - Unipolar
  JP1 = Header 6 [package=molex-1x6_lock]
  JP2 = Header 6 [package=molex-1x6_lock]
  JP3 = Header 2 [package=springterminal-2.54mm-2]
  JP4 = Header 2 [package=springterminal-2.54mm-2]
  JP5 = Header 6 [package=1x06-smd-female-v2]
  JP6 = Header 6 [package=1x06-smd-female-v2]
  JP7 = Header 1 [package=luxeon-pad]
  JP8 = Header 1 [package=luxeon-pad]
  S1 = SWITCH-MOMENTARY-2 [package=tactile-pth-12mm]
  S2 = SWITCH-MOMENTARY-2 [package=tactile-pth-12mm]
  R1 = Resistor [tolerance=±5% resistance=220 package="0603 [SMD]"]
  servo = Basic Servo
  R2 = Resistor [tolerance=±5% resistance=220 package=THT]
  J1 = female pin header, 2 pins [form="♀ (female)"]
  J2 = female pin header, 2 pins [form="♀ (female)"]

nets:
  N1: Part1.D8, Push.BIN2
  N2: Part1.D9_PWM, Push.BIN1
  N3: Part1.D10_PWM/SS, Push.AIN1
  N4: Part1.D11_PWM/MOSI, Push.AIN2
  N5: Part1.D12/MISO, J1.pin1
  N6: Part1.D2, JP2.3
  VCC: Part1.D3_PWM, Push.VCC, Push.PWMA, Push.PWMB, Lift.VCC, Lift.PWMA, Lift.PWMB, JP1.6, JP2.4, JP4.1, JP5.1, JP5.3, JP5.6
  N7: Part1.D4, Lift.BIN2
  N8: Part1.D5_PWM, Lift.BIN1
  N9: Part1.D6_PWM, Lift.AIN1
  N10: Part1.D7, Lift.AIN2
  N11: Part1.5V, JP2.1
  N12: Part1.VIN, JP2.2
  GND: Push.GND, Lift.GND, JP1.2, JP5.5, R1.Pin_0, R2.Pin_0
  N13: Push.B01, Push_2.D
  N14: Push.B02, Push_2.C
  N15: Push.A02, Push_2.B
  N16: Push.A01, Push_2.A
  N17: Push.VM, Lift.VM, JP3.1, JP3.2
  N18: Lift.B01, Lift_2.A
  N19: Lift.B02, Lift_2.B
  N20: Lift.A02, Lift_2.D
  N21: Lift.A01, Lift_2.C
  N22: JP1.3, JP5.4, R1.Pin_1
  N23: JP1.4, JP5.2, R2.Pin_1
  N24: JP1.5, JP4.2, J2.pin2
  N25: JP6.1, S2.2
  N26: JP6.2, S2.1
  N27: JP6.3, S1.1
  N28: JP6.4, S1.2
  N29: JP6.5, servo.vcc
  N30: JP6.6, servo.pulse
  N31: JP7.1, J2.pin1
  N32: JP8.1, servo.gnd
