# Fritzing sketch AIT Final Diagram (saved by Fritzing 0.9.3b)
breadboards: 1

parts:
  JP2 = Header 10 [package=1x10-2mm-smd]
  JP4 = Header 10 [package=1x10-2mm-smd]
  JP7 = Header 6 [package=1x06_smd_straight_alt]
  JP9 = Header 6 [package=1x06_smd_straight_alt]
  JP10 = Header 6 [package=1x06_smd_straight_alt]
  JP12 = Header 2 [package=springterminal-2.54mm-2]
  JP14 = Header 2 [package=springterminal-2.54mm-2]
  JP16 = Header 2 [package=springterminal-2.54mm-2]
  JP18 = Header 2 [package=springterminal-2.54mm-2]
  Arduino = Arduino Uno (Rev3)
  JP20 = Header 2 [package=springterminal-2.54mm-2]  # not connected
  JP21 = Header 2 [package=springterminal-2.54mm-2]
  JP25 = Header 3 [package=screwterminal-3.5mm-3_lock.007s]
  JP27 = Header 4 [package=screwterminal-3.5mm-4_lock]
  JP29 = Header 2 [package=springterminal-2.54mm-2]
  JP31 = Header 2 [package=springterminal-2.54mm-2]
  JP33 = Header 2 [package=springterminal-2.54mm-2]
  JP35 = Header 2 [package=springterminal-2.54mm-2]
  PUSH_motor = Stepper Motor - Bipolar
  LIFT_motor = Stepper Motor - Bipolar
  Blue_Button-_solid = Pushbutton [package="[THT]"]
  Green_Button-_liquid = Pushbutton [package="[THT]"]
  Servo = Basic Servo
  JP36 = Header 2 [package=springterminal-2.54mm-2]

nets:
  N1: JP2.1, JP4.1
  N2: JP2.2, JP2.4, JP2.10, JP4.2, JP4.4, JP4.10, JP10.1, JP10.2, Arduino.D13/SCK, JP21.2, JP36.1, JP36.2
  N3: JP2.3, JP4.3, JP10.5, Arduino.GND, Arduino.D0/RX, Arduino.D1/TX, JP21.1, Blue_Button-_solid.Pin_3, Blue_Button-_solid.Pin_4, Green_Button-_liquid.Pin_3, Green_Button-_liquid.Pin_4
  N4: JP2.5, JP14.1, Arduino.D11_PWM/MOSI
  N5: JP7.1, JP35.1, PUSH_motor.A
  N6: JP7.2, JP35.2, PUSH_motor.C
  N7: JP7.5, JP33.1, PUSH_motor.B
  N8: JP7.6, JP33.2, PUSH_motor.D
  N9: JP9.1, JP29.2, LIFT_motor.D
  N10: JP9.2, JP29.1, LIFT_motor.B
  N11: JP9.5, JP31.2, LIFT_motor.C
  N12: JP9.6, JP31.1, LIFT_motor.A
  N13: JP10.3, Arduino.D3_PWM
  N14: JP10.4, Arduino.D2
  N15: JP10.6, Arduino.D12/MISO
  N16: JP12.1, Arduino.D5_PWM
  N17: JP12.2, Arduino.D4
  N18: JP14.2, Arduino.D10_PWM/SS
  N19: JP16.1, Arduino.D9_PWM
  N20: JP16.2, Arduino.D8
  N21: JP18.1, Arduino.D7
  N22: JP18.2, Arduino.D6_PWM
  N23: JP25.1, Servo.vcc
  N24: JP25.2, Servo.pulse
  N25: JP25.3, Servo.gnd
  N26: JP27.1, JP27.2, JP27.3, JP27.4, Blue_Button-_solid.Pin_1, Blue_Button-_solid.Pin_2, Green_Button-_liquid.Pin_1, Green_Button-_liquid.Pin_2
