# Fritzing sketch AIT Schematic 180215 (saved by Fritzing 0.9.3b)
breadboards: 1

parts:
  PWMA2 = DIP - 20 pins [chip_label=IC package="DIP (Dual Inline) [THT]"]
  Motor1 = Stepper Motor - Bipolar
  PWMA1 = DIP - 20 pins [chip_label=IC package="DIP (Dual Inline) [THT]"]
  Motor2 = Stepper Motor - Bipolar
  Part1 = Arduino Uno (Rev3)
  B2 = Pushbutton [package="[THT]"]
  B1 = Pushbutton [package="[THT]"]
  R1 = Resistor [tolerance=±5% resistance=10k package=THT]
  R2 = Resistor [tolerance=±5% resistance=10k package=THT]

nets:
  N1: PWMA2.pin1, Motor2.D
  N2: PWMA2.pin3, Motor2.C
  N3: PWMA2.pin6, Motor2.A
  N4: PWMA2.pin7, Motor2.B
  N5: PWMA2.pin11, PWMA2.pin13, PWMA1.pin11, PWMA1.pin13, R1.Pin_1, R2.Pin_1
  N6: PWMA2.pin12, PWMA2.pin14#13, PWMA2.pin16#19, PWMA1.pin12, PWMA1.pin14#13, PWMA1.pin16#19, Part1.VIN, B2.Pin_1, B2.Pin_2, B1.Pin_1, B1.Pin_2
  N7: PWMA2.pin15#14, Part1.D11_PWM/MOSI
  N8: PWMA2.pin16#15, Part1.D10_PWM/SS
  N9: PWMA2.pin14#17, Part1.D9_PWM
  N10: PWMA2.pin15#18, Part1.D8
  N11: Motor1.A, PWMA1.pin6
  N12: Motor1.C, PWMA1.pin3
  N13: Motor1.B, PWMA1.pin7
  N14: Motor1.D, PWMA1.pin1
  N15: PWMA1.pin15#14, Part1.D7
  N16: PWMA1.pin16#15, Part1.D6_PWM
  N17: PWMA1.pin14#17, Part1.D5_PWM
  N18: PWMA1.pin15#18, Part1.D4
  N19: Part1.D2, B1.Pin_3, B1.Pin_4, R2.Pin_0
  N20: Part1.D3_PWM, B2.Pin_3, B2.Pin_4, R1.Pin_0

custom parts:
  DIP - 20 pins: A DIP stand-in part for whatever IC you want. With 20 pins on a 300mil dual inline package (DIP) footprint.
