# Fritzing sketch Petrolab Watlow Controller Box (saved by Fritzing 0.9.3b)
breadboards: 1

parts:
  U1 = Petrolab Watlow Controller Box Solid State Relay [package=g3vm-61e1]  # not connected
  U2 = Petrolab Watlow Controller Box Solid State Relay [package=g3vm-61e1]  # not connected
  U3 = Petrolab Watlow Controller Box Solid State Relay [package=g3vm-61e1]
  J1 = screw terminal, 5 pins
  J2 = screw terminal, 5 pins
  J3 = Screw terminal - 2 pins [package=THT]
  Yellow_Cord = female pin header, 2 pins [form="♀ (female)"]
  White_Cord = female pin header, 2 pins [form="♀ (female)"]
  Black_Cord = female pin header, 3 pins [form="♀ (female)"]
  Switch = double row female pin header, 2 pins [form="♀ (female)"]
  J4 = female pin header, 2 pins [form="♀ (female)"]
  J5 = female pin header, 2 pins [form="♀ (female)"]

nets:
  N1: U3.4, Black_Cord.pin3
  N2: U3.3, J1.pin2
  N3: U3.2, White_Cord.pin2
  N4: U3.GND, J4.pin2
  N5: U3.1, J1.pin1
  N6: J2.pin3, Yellow_Cord.pin2
  N7: J2.pin5, Yellow_Cord.pin1
  N8: J3.pin1, J4.pin1
  N9: J3.pin2, J5.pin2
  N10: White_Cord.pin1, J5.pin1
  N11: Black_Cord.pin1, Switch.pin1
  N12: Black_Cord.pin2, Switch.pin2

custom parts:
  Petrolab Watlow Controller Box Solid State Relay: Omron NO solid state relay
