# Fritzing sketch Petrolab Watlow Controller Box (saved by Fritzing 0.9.3b)
breadboards: 1

parts:
  U1 = Petrolab Watlow Controller Box Solid State Relay [package=g3vm-61e1]  # not connected
  U2 = Petrolab Watlow Controller Box Solid State Relay [package=g3vm-61e1]  # not connected
  U3 = Petrolab Watlow Controller Box Solid State Relay [package=g3vm-61e1]
  J1 = screw terminal, 5 pins
  J2 = screw terminal, 5 pins
  J3 = Screw terminal - 2 pins [package=THT]
  Yellow_Cord(Thermocouple_to_furnace) = female pin header, 2 pins [form="♀ (female)"]
  White_Cord_(Power_to_furnace) = female pin header, 2 pins [form="♀ (female)"]
  Black_Cord_(Power_from_wall) = female pin header, 3 pins [form="♀ (female)"]
  South = double row female pin header, 2 pins [form="♀ (female)"]
  East = female pin header, 2 pins [form="♀ (female)"]
  West = female pin header, 2 pins [form="♀ (female)"]
  LED1 = LED - 5mm [color="Red (633nm)" package="5 mm [THT]"]

nets:
  N1: U3.4, Black_Cord_(Power_from_wall).pin3
  N2: U3.3, J1.pin2
  N3: U3.2, White_Cord_(Power_to_furnace).pin2
  N4: U3.GND, East.pin2
  N5: U3.1, J1.pin1
  N6: J2.pin3, Yellow_Cord(Thermocouple_to_furnace).pin2
  N7: J2.pin5, Yellow_Cord(Thermocouple_to_furnace).pin1
  N8: J3.pin1, East.pin1, LED1.cathode
  N9: J3.pin2, West.pin2, LED1.anode
  N10: White_Cord_(Power_to_furnace).pin1, West.pin1
  N11: Black_Cord_(Power_from_wall).pin1, South.pin1
  N12: Black_Cord_(Power_from_wall).pin2, South.pin2

notes:
  Grey wires are white
  Switch Nomeclature
  Top is marked with tape. This is the Northeast corner. Others are labeled with respect to this corner.
  Negative thermocouple goes to number 5

custom parts:
  Petrolab Watlow Controller Box Solid State Relay: Omron NO solid state relay
