# Fritzing sketch tada_wireing (saved by Fritzing 0.9.3b)
circuit board: 9.00231cm x 6.91926cm
breadboards: 1

parts:
  interface_header = Header 4 [package=1x04-smd]
  lvl_convert_l = Header 6 [package=1x06_smd_straight_alt]
  lvl_convert_r = Header 6 [package=1x06_smd_straight_alt]
  T0 = Header 8 [package=1x08_smd_combined]
  T3 = Header 8 [package=1x08_smd_combined]
  T1 = Header 8 [package=1x08_smd_combined]
  T2 = Header 8 [package=1x08_smd_combined]
  R1 = Resistor [tolerance=±5% resistance=4.7k package="0603 [SMD]"]

nets (from the schematic view):
  N1: interface_header.1, lvl_convert_l.6, T0.7, T3.7, T1.7, T2.7
  N2: interface_header.2, lvl_convert_r.6, T0.8, T3.8, T1.8, T2.8
  N3: interface_header.3, lvl_convert_r.1, R1.Pin_1
  N4: interface_header.4, lvl_convert_l.5
  N5: lvl_convert_r.2, T0.1, T3.1, T1.1, T2.1, R1.Pin_0
