# Fritzing sketch TADA_Final_Diagram (saved by Fritzing 0.9.3b)
breadboards: 1

parts:
  DATA = Header 1 [package=snap-female]
  A3 = Header 1 [package=snap-female]  # not connected
  A2 = Header 1 [package=snap-female]  # not connected
  A1 = Header 1 [package=snap-female]  # not connected
  A0 = Header 1 [package=snap-female]  # not connected
  3V3 = Header 1 [package=snap-female]  # not connected
  VIN = Header 1 [package=snap-female]
  GND = Header 1 [package=snap-female]
  DATA_2 = Header 1 [package=snap-female]
  A3_2 = Header 1 [package=snap-female]  # not connected
  A2_2 = Header 1 [package=snap-female]  # not connected
  A1_2 = Header 1 [package=snap-female]  # not connected
  A0_2 = Header 1 [package=snap-female]  # not connected
  3V3_2 = Header 1 [package=snap-female]  # not connected
  VIN_2 = Header 1 [package=snap-female]
  GND_2 = Header 1 [package=snap-female]
  DATA_3 = Header 1 [package=snap-female]
  DATA_4 = Header 1 [package=snap-female]
  A3_3 = Header 1 [package=snap-female]  # not connected
  A3_4 = Header 1 [package=snap-female]  # not connected
  A2_3 = Header 1 [package=snap-female]  # not connected
  A2_4 = Header 1 [package=snap-female]  # not connected
  A1_3 = Header 1 [package=snap-female]  # not connected
  A1_4 = Header 1 [package=snap-female]  # not connected
  A0_3 = Header 1 [package=snap-female]  # not connected
  A0_4 = Header 1 [package=snap-female]  # not connected
  3V3_3 = Header 1 [package=snap-female]  # not connected
  3V3_4 = Header 1 [package=snap-female]  # not connected
  VIN_3 = Header 1 [package=snap-female]
  VIN_4 = Header 1 [package=snap-female]
  GND_3 = Header 1 [package=snap-female]
  GND_4 = Header 1 [package=snap-female]
  GND_5 = Header 1 [package=snap-female]  # not connected
  B4 = Header 1 [package=snap-female]  # not connected
  B3 = Header 1 [package=snap-female]  # not connected
  B2 = Header 1 [package=snap-female]  # not connected
  B1 = Header 1 [package=snap-female]
  HV = Header 1 [package=snap-female]  # not connected
  GND_6 = Header 1 [package=snap-female]
  A4 = Header 1 [package=snap-female]  # not connected
  A3_5 = Header 1 [package=snap-female]  # not connected
  A2_5 = Header 1 [package=snap-female]  # not connected
  A1_5 = Header 1 [package=snap-female]
  LV = Header 1 [package=snap-female]
  JP1 = Header 1 [package=snap-female]
  JP2 = Header 1 [package=snap-female]
  JP3 = Header 1 [package=snap-female]
  JP4 = Header 1 [package=snap-female]
  R1 = Resistor [tolerance=±5% resistance=4.7k package="0603 [SMD]"]
  JP5 = Header 1 [package=smtso-256-et]
  JP6 = Header 1 [package=smtso-256-et]
  JP7 = Header 1 [package=smtso-256-et]
  JP8 = Header 1 [package=smtso-256-et]
  Part1 = Arduino Mega 2560 (Rev3)
  U2 = LM124-324 Quad Opamp [package="DIP (Dual Inline)"]
  R2 = Resistor [tolerance=±5% resistance=82 package=THT]
  R3 = Resistor [tolerance=±5% resistance=180 package=THT]
  Pressure_Transducer = Header 1 [package=snap-female]
  A6 = Header 1 [package=snap-female]
  A7 = Header 1 [package=snap-female]
  24V_Source = Power plug

nets:
  N1: DATA.1, DATA_2.1, DATA_3.1, DATA_4.1, A1_5.1, R1.Pin_0
  N2: VIN.1, VIN_2.1, VIN_3.1, VIN_4.1, JP1.1
  N3: GND.1, GND_2.1, GND_3.1, GND_4.1, GND_6.1, JP2.1, U2.VCC-, R3.Pin_1, A7.1, 24V_Source.GND
  N4: B1.1, JP4.1
  N5: LV.1, JP3.1, R1.Pin_1
  N6: JP5.1, Part1.IOREF
  N7: JP6.1, Part1.GND
  N8: JP7.1, Part1.3V3
  N9: JP8.1, Part1.D2_PWM
  N10: Part1.A0, U2.4IN-, U2.4OUT
  N11: U2.VCC+, A6.1, 24V_Source.VCC
  N12: U2.4IN+, R2.Pin_0, Pressure_Transducer.1
  N13: R2.Pin_1, R3.Pin_0
